# Fritzing sketch AutomationsESP32 (saved by Fritzing 0.9.3b)
breadboards: 2

parts:
  U1 = ESP32-38PinWide [part_number=ESP32-38PinWide]
  Part1 = Black Joystick KY-023
  DHT1 = Humidity and Temperature Sensor DHT11
  Power_plug1 = Power plug
  R1 = Resistor [tolerance=±5% resistance=10k package=THT]
  LCD2004-I2C1 = LCD2004-I2C
  Keypad4x1 = Keypad Membran 4x4  # not connected
  8_Channel_Relay1 = 8 Channel Power Relay  # not connected

nets:
  N1: U1.3.3, Part1.+5V
  N2: U1.GPIO32, Part1.VRy
  N3: U1.GPIO33, Part1.VRx
  N4: U1.GPIO14, Part1.SW
  GND: U1.GND, Part1.GND, DHT1.GND_2, Power_plug1.GND, LCD2004-I2C1.GND
  VIN: U1.VIN, LCD2004-I2C1.VCC
  VCC: DHT1.Vcc, Power_plug1.VCC, R1.Pin_0
  N5: DHT1.Data-signal, R1.Pin_1

custom parts:
  ESP32-38PinWide: Generic 38-Pin ESP32 with wide format (only access to one side of pins on a breadboard) based on Stephen Lilley's HiLetgo ESP-WROOM-32 ESP32 ESP-32S Development Board.
  Black Joystick KY-023: Description: The joystick is a combination of 2 analoog potentiometer and a digital switch. Arduino GND --> Module pin - Arduino +5V --> Module pin +5V Arduino Analoog 0 --> Module VRx Arduino Analoog 1 --> Module VRy Arduino Digital --> Module SW Dimensions: 1" x 1.25"
  Humidity and Temperature Sensor DHT11: Digital relative humidity & temperature sensor DHT11
  LCD2004-I2C: A standard character display with 4x20 characters. Comes in many colors with LCM2004 IIC attached.
  Keypad Membran 4x4: Membrane Keypad 4x4 Matrix
  8 Channel Power Relay: An 8 channel power relay. The module operates at 5V.
